# Fritzing sketch blink (saved by Fritzing 0.9.2b)
breadboards: 1

parts:
  Part1 = Arduino Uno (Rev3)
  LED1 = LED - 5mm [color="Red (633nm)" package="5 mm [THT]"]

nets:
  N1: Part1.D12/MISO, LED1.anode
  N2: Part1.GND, LED1.cathode

// code stored in the sketch: blink.ino
void setup() {
  // put your setup code here, to run once:
	pinMode(12, OUTPUT);

}

void loop() {
  // put your main code here, to run repeatedly:
 digitalWrite(12, HIGH);   // turn the LED on (HIGH is the voltage level)
  delay(1000);              // wait for a second
  digitalWrite(12, LOW);    // turn the LED off by making the voltage LOW
  delay(1000);   
}
